# Fritzing sketch 20210116_sketch (saved by Fritzing 0.9.4)
breadboards: 1

parts:
  R1 = Trimmer Potentiometer [maximum_resistance=10kΩ package=THT]
  SP1 = SPEAKER [package=pcb_mount_speaker]
  U1 = AD8541 - CMOS Rail-to-Rail Op Amp [part_number=AD8541]
  R2 = Rotary Potentiometer (Small) [maximum_resistance=100kΩ package=THT]
  R3 = Rotary Potentiometer (Small) [maximum_resistance=100kΩ package=THT]
  ADC2 = MCP3008 [package=dil16]
  MCU1 = Raspberry Pi Zero

nets:
  GND: R1.leg1, SP1.+, U1.-V, R2.leg1, R3.leg1, ADC2.DGND, ADC2.AGND, MCU1.pin_6, MCU1.pin_20, MCU1.pin_39
  N1: R1.wiper, U1.+INA
  N2: R1.leg2, MCU1.pin_33
  N3: SP1.-, U1.OUTA
  N4: U1.-INA, MCU1.pin_12
  5V: U1.V+, R2.leg2, R3.leg2, ADC2.VREF, ADC2.VDD, MCU1.pin_1, MCU1.pin_17
  N5: R2.wiper, ADC2.CH0
  N6: R3.wiper, ADC2.CH1
  N7: ADC2.CS/SHDN, MCU1.pin_24
  N8: ADC2.Din, MCU1.pin_19
  N9: ADC2.Dout, MCU1.pin_21
  N10: ADC2.CLK, MCU1.pin_23
